# Fritzing sketch schematicfinal (saved by Fritzing 0.9.2b)
breadboards: 3

parts:
  Ultrasonic_Sensor = HC-SR04 Ultrasonic Rangemeter
  R2 = PHOTOCELL [package=photocell-kit]
  R3 = PHOTOCELL [package=photocell-kit]
  R4 = PHOTOCELL [package=photocell-kit]
  Part3 = Arduino Mega 2560 (Rev3)
  R5 = PHOTOCELL [package=photocell-kit]
  R7 = Resistor [tolerance=±5% resistance=470 package="0402 [SMD]"]
  R8 = Resistor [tolerance=±5% resistance=470 package="0402 [SMD]"]
  R9 = Resistor [tolerance=±5% resistance=470 package="0402 [SMD]"]
  R10 = Resistor [tolerance=±5% resistance=470 package="0402 [SMD]"]
  LED1 = LEDs [package=led10mm]
  LED2 = LEDs [package=led10mm]
  LED3 = LEDs [package=led10mm]
  LED4 = LEDs [package=led10mm]
  R11 = Resistor [tolerance=±5% resistance=220 package=THT]
  R12 = Resistor [tolerance=±5% resistance=220 package=THT]
  R13 = Resistor [tolerance=±5% resistance=220 package=THT]
  R14 = Resistor [tolerance=±5% resistance=220 package=THT]
  3-Axis_Accelerometer1 = 3-Axis Accelerometer Breakout - MMA8452Q
  SP1 = SPEAKER [package=pcb_mount_speaker]

nets:
  N1: Ultrasonic_Sensor.VCC, Part3.IOREF
  N2: Ultrasonic_Sensor.Trig, Part3.D8_PWM
  N3: Ultrasonic_Sensor.Echo, Part3.D9_PWM
  GND: Ultrasonic_Sensor.GND, R2.P$1, R3.P$1, R4.P$1, Part3.A1, Part3.A2, Part3.A3, Part3.A4, Part3.GND, R5.P$1, R7.Pin_0, R7.Pin_1, R8.Pin_0, R8.Pin_1, R9.Pin_0, R9.Pin_1, R10.Pin_0, R10.Pin_1, LED1.A, LED2.A, LED3.A, LED4.A, R11.Pin_0, R11.Pin_1, R12.Pin_0, R12.Pin_1, R13.Pin_0, R13.Pin_1, R14.Pin_0, R14.Pin_1, 3-Axis_Accelerometer1.GND, SP1.-
  N4: R2.P$2, R3.P$2, R4.P$2, Part3.5V, R5.P$2
  N5: Part3.SCL, 3-Axis_Accelerometer1.SCL
  N6: Part3.SDA, 3-Axis_Accelerometer1.SDA
  N7: Part3.D13_PWM, SP1.+
  3V3: Part3.3V3, 3-Axis_Accelerometer1.3.3V
  N8: Part3.D4_PWM, LED1.C
  N9: Part3.D5_PWM, LED2.C
  N10: Part3.D6_PWM, LED3.C
  N11: Part3.D7_PWM, LED4.C
